// Digital circuit modulo.dig as structural Verilog
module modulo (
  input  [4:0] S0,
  output [4:0] modlo
);

  wire sinal_1_sinal;
  wire [4:0] neg_1_out, relaydt_1_p4, relaydt_1_p5;

  sinal sinal_1 (.S0(S0), .Sinal(sinal_1_sinal));
  // RelayDT #(.Bits(5)) relaydt_1: pin names not known; wires that end beside it: sinal_1_sinal, S0, 1'b0, relaydt_1_p4, relaydt_1_p5
  Neg #(.Bits(5)) neg_1 (.in(relaydt_1_p4), .out(neg_1_out));
  assign modlo = neg_1_out | relaydt_1_p5;  // Or or_1, 5 bits wide
endmodule
